# Fritzing sketch carro autonomo (saved by Fritzing 0.9.3b)

parts:
  L298N1 = L298N DC motor driver
  M1 = DC Motor
  M2 = DC Motor
  U1 = LIPO-2000mAh [package=lipo-2000]
  U2 = LIPO-2000mAh [package=lipo-2000]
  M3 = DOIT Esp32 DevKit v1 (30 pins long, 11 pins width) [part_number=ESP32S-PIN30]
  Componente1 = SRF05 Ultrasonic Rangefinder
  Componente2 = SRF05 Ultrasonic Rangefinder
  Componente3 = SRF05 Ultrasonic Rangefinder

nets:
  N1: L298N1.OUT1, M2.pin_2
  N2: L298N1.OUT2, M2.pin_1
  N3: L298N1.OUT3, M1.pin_2
  N4: L298N1.OUT4, M1.pin_1
  N5: L298N1.12V, U1.+
  GND: L298N1.GND, U2.-, M3.GND, Componente1.GND, Componente2.GND
  VCC: L298N1.5V, M3.VIN, Componente1.VCC, Componente2.VCC, Componente3.VCC
  N6: L298N1.ENA, M3.D12
  N7: L298N1.ENB, M3.D13
  N8: L298N1.IN1, M3.D2
  N9: L298N1.IN2, M3.D4
  N10: L298N1.IN3, M3.D18
  N11: L298N1.IN4, M3.D19
  N12: U1.-, U2.+
  N13: M3.D21, Componente3.Echo
  N14: M3.D23, Componente1.Trig
  N15: M3.D35, Componente2.Echo
  N16: M3.D32, Componente2.Trig
  N17: M3.D26, Componente1.Echo
  N18: M3.D27, Componente3.Trig

notes:
  2 x 3.7 V LiPo Batteries connected in series
  Motor de traccion
  Motor direccion
  puente h l298n

custom parts:
  L298N DC motor driver: 2x DC motor driver with 78M05 positive voltage regulator (7..35 V) L298N: max 46 V, 2 A Set 5 V Enable jumper to enable 5 V regultor (needed for the L298N) and +5 V output at screw terminal or supply external +5 V at screw terminal Set ENA and/or ENB to +5 V to enable motor permanently or supply ENA and/or ENB with PWM signal IN1 and IN2 set rotation directory for motor A (OUT1/OUT2) IN2 and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
  DOIT Esp32 DevKit v1 (30 pins long, 11 pins width): The DOIT Esp32 DevKit v1 is one of the development board created by DOIT to evaluate the ESP-WROOM-32 module. It is based on the ESP32 microcontroller that boasts Wifi, Bluetooth, Ethernet and Low Power support all in a single chip. (vanepp) made breadboard work, adjusted pin numbering and labels and reduced size of schematic and cleaned up pcb. This chip is 30pins long (2 x15) and 11 pins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
